// Logisim project mmarc-12.circ as structural Verilog
module alu (
  input  [19:0] in_a,
  input  [19:0] in_b,
  input  [2:0] op,
  output [19:0] out_c
);

  wire [19:0] adder_1_out, AND_out, OR_out, subtractor_1_out, XOR_out;

  Adder #(.width(20)) adder_1 (.a(in_a), .b(in_b), .out(adder_1_out));  // open: cin, cout
  Subtractor #(.width(20)) subtractor_1 (.a(in_a), .b(in_b), .out(subtractor_1_out));  // open: bin, bout
  assign OR_out = in_a | in_b;  // OR_Gate OR, 20 bits wide
  assign AND_out = in_a & in_b;  // AND_Gate AND, 20 bits wide
  assign XOR_out = in_a ^ in_b;  // XOR_Gate XOR, 20 bits wide
  Multiplexer #(.select(3), .width(20)) multiplexer_1 (
    .in0(adder_1_out), .in1(subtractor_1_out), .in2(OR_out), .in3(AND_out), .in4(XOR_out), .in5({20{1'b0}}),
    .in6({20{1'b0}}), .in7({20{1'b0}}), .out(out_c), .sel(op), .en(1'b1));
endmodule

module control_logic (
  input  b3,
  input  b2,
  input  b1,
  input  b0,
  output branch,
  output branch_type,
  output mem_select,
  output write_enable,
  output write_flags,
  output write_accum,
  output alu_src,
  output mem_in_sel,
  output accum_in_sel,
  output mem_offset,
  output mem_write_sel,
  output alu_op2,
  output alu_op1,
  output alu_op0
);

  wire and_5_out, and_6_out, and_7_out, and_9_out, and_10_out, and_12_out, and_13_out, and_14_out,
       and_15_out, not_1_out, not_2_out, not_3_out, not_4_out, not_5_out, not_6_out, not_7_out, not_8_out,
       not_9_out, not_10_out, not_11_out, not_12_out, not_13_out, not_14_out, not_15_out, not_16_out,
       not_17_out, not_18_out, not_19_out;

  not not_1 (not_1_out, b1);
  and and_1 (alu_op1, b2, b1);
  not not_2 (not_2_out, b3);
  not not_3 (not_3_out, b1);
  not not_4 (not_4_out, b0);
  and and_2 (branch, b3, b2);
  not not_5 (not_5_out, b1);
  not not_6 (not_6_out, b3);
  not not_7 (not_7_out, b2);
  not not_8 (not_8_out, b1);
  not not_9 (not_9_out, b0);
  not not_10 (not_10_out, b2);
  not not_11 (not_11_out, b2);
  not not_12 (not_12_out, b1);
  not not_13 (not_13_out, b3);
  not not_14 (not_14_out, b3);
  not not_15 (not_15_out, b3);
  not not_16 (not_16_out, b2);
  not not_17 (not_17_out, b0);
  not not_18 (not_18_out, b3);
  not not_19 (not_19_out, b2);
  and and_3 (accum_in_sel, b3, b1);
  not not_20 (mem_offset, b0);
  and and_4 (alu_op2, b2, not_1_out, b0);
  and and_5 (and_5_out, not_2_out, not_3_out, not_4_out);
  and and_6 (and_6_out, b1, b0);
  and and_7 (and_7_out, b3, b0);
  and and_8 (branch_type, not_5_out, b0);
  and and_9 (and_9_out, not_6_out, not_7_out, not_8_out, not_9_out);
  and and_10 (and_10_out, b3, not_10_out, b1, b0);
  and and_11 (write_flags, b3, not_11_out, not_12_out, b0);
  and and_12 (and_12_out, not_13_out, b0);
  and and_13 (and_13_out, not_14_out, b1);
  and and_14 (and_14_out, not_15_out, b2);
  and and_15 (and_15_out, b3, not_16_out, not_17_out);
  and and_16 (alu_src, not_18_out, not_19_out, b0);
  or or_1 (alu_op0, and_5_out, and_6_out, and_7_out);
  or or_2 (write_enable, and_9_out, and_10_out);
  or or_3 (write_accum, and_12_out, and_13_out, and_14_out, and_15_out);

  assign mem_in_sel = b3;
  assign mem_select = b3;
  assign mem_write_sel = b3;
endmodule
